# Fritzing sketch router cooling exp (saved by Fritzing 0.9.5d)
circuit board: 5.1636cm x 6.30756cm
breadboards: 1

parts:
  H1 = polarizedheader 4pin 0.156in [package=THT]
  JP1 = Header 2 [package=jst-2-pth-kit]
  R1 = Resistor [tolerance=±5% resistance=10k package=THT]
  JP2 = Header 2 [package=jst-2-pth]
  D1 = Rectifier Diode [part_number=1N4001 package="300 mil [THT]"]
  Teensy_3_2 = Teensy 3.1

nets:
  N1: H1.pin1, JP1.2, Teensy_3_2.GND
  N2: H1.pin2, JP1.1
  N3: H1.pin3, D1.cathode
  N4: H1.pin4, Teensy_3_2.D4
  N5: R1.Pin_0, Teensy_3_2.3V3, Teensy_3_2.3V3.2, Teensy_3_2.AREF
  N6: R1.Pin_1, JP2.1, Teensy_3_2.A5/D19
  N7: JP2.2, Teensy_3_2.AGND
  N8: D1.anode, Teensy_3_2.D5

notes:
  Fan Header
  12v power header
  Sensor header
  Router cooling demo
  (Teensy Fan Controller)
  Teensy Fan Controller

custom parts:
  Teensy 3.1: The Teensy is a complete USB-based microcontoller development system, in a very small footprint, capable of implementing many types of projects. All programming is done via the USB port. No special programmer is needed, only a standard micro-USB cable and a PC or Macintosh with a USB port. It has a USB keyboard/mouse/joystick emulation stack and can be programmed through Arduino IDE.
